// Logisim project SAP-1.circ as structural Verilog: 19 circuits, main circuit main
// Sv
module main (
  input  Reset,
  output [3:0] \Endereço ,
  output [3:0] Dados,
  output out_4,
  output out_5,
  output out_6,
  output out_7,
  output out_8,
  output out_9,
  output out_10,
  output out_11
);

  wire Ar, CLK, Clock_out, controlador_sequencializador_1_hlt, Cp, Dv, Ea, Eb, Ep, Eq, Eu, Gr, Lo, Mu, nCE,
       nEi, nLa, nLb, nLi, nLm, nLo, not_1_out, not_2_out, not_3_out, not_4_out,
       \registrador_instruções_1_i4 , \registrador_instruções_1_i5 , \registrador_instruções_1_i6 ,
       \registrador_instruções_1_i7 , Su, Sv;
  wire [3:0] rem_1_remout;
  wire [7:0] acumulador_1_a_out_ula, registrador_b_1_b_out_ula;

  Clock Clock (.out(Clock_out));
  not not_1 (not_1_out, CLK);
  not not_2 (not_2_out, Reset);
  not not_3 (not_3_out, nCE);
  assign CLK = not_4_out ? Clock_out : 1'bz;  // Controlled_Buffer controlled_buffer_1
  not not_4 (not_4_out, controlador_sequencializador_1_hlt);
  REM rem_1 (.in_1(Dados), .nLm(nLm), .CLK(CLK), .REMOut(rem_1_remout));
  Contador_Programa contador_programa_1 (
    .Cp(Cp), .nCLK(not_1_out), .nCLR(not_2_out), .Ep(Ep), .Cp_Out(Dados), .in_2(Dados), .Ar(Ar));
  \Memória_RAM  \memória_ram_1  (
    .in_1(rem_1_remout), .nCE(not_3_out), .CLK(CLK), .out_6({\Endereço , Dados}), .Sv(Sv),
    .in_2({\Endereço , Dados}));
  \Registrador_Instruções  \registrador_instruções_1  (
    .in_1({\Endereço , Dados}), .nLi(nLi), .CLK(CLK), .CLR(Reset), .nEi(nEi), .out_6({\Endereço , Dados}),
    .I4(\registrador_instruções_1_i4 ), .I5(\registrador_instruções_1_i5 ),
    .I6(\registrador_instruções_1_i6 ), .I7(\registrador_instruções_1_i7 ));
  Controlador_Sequencializador controlador_sequencializador_1 (
    .CLR(Reset), .I7(\registrador_instruções_1_i7 ), .Ep(Ep), .Cp(Cp), .I6(\registrador_instruções_1_i6 ),
    .I5(\registrador_instruções_1_i5 ), .I4(\registrador_instruções_1_i4 ),
    .HLT(controlador_sequencializador_1_hlt), .nLm(nLm), .nCE(nCE), .nEl(nEi), .nLa(nLa), .Ea(Ea), .Su(Su),
    .Eu(Eu), .nLb(nLb), .nLo(nLo), .nLl(nLi), .CLK(CLK), .Ar(Ar), .Gr(Gr), .Lo(Lo), .Eq(Eq), .Eb(Eb),
    .Sv(Sv), .Mu(Mu), .Dv(Dv));
  Acumulador acumulador_1 (
    .A_In({\Endereço , Dados}), .nLa(nLa), .CLK(CLK), .Ea(Ea), .A_Out_ULA(acumulador_1_a_out_ula),
    .A_Out({\Endereço , Dados}));
  Somador_Subtrator somador_subtrator_1 (
    .Su(Su), .B_data(registrador_b_1_b_out_ula), .A_dataOut2({\Endereço , Dados}),
    .A_data(acumulador_1_a_out_ula), .Eu(Eu), .Gr(Gr), .Lo(Lo), .Eq(Eq), .Mu(Mu), .Dv(Dv));
  Registrador_B registrador_b_1 (
    .B_dataIn({\Endereço , Dados}), .B_out_ULA(registrador_b_1_b_out_ula), .nLb(nLb), .CLK(CLK), .Eb(Eb),
    .B_out({\Endereço , Dados}));
  Hex_Digit_Display hex_digit_display_1 (.value({out_4, out_5, out_6, out_7}));  // open: dp
  \Indicação_Visual  \indicação_visual_1  (
    .Input({\Endereço , Dados}), .Output({out_4, out_5, out_6, out_7, out_8, out_9, out_10, out_11}),
    .nLo(nLo), .CLK(CLK), .CLR(Reset));
  Hex_Digit_Display hex_digit_display_2 (.value({out_8, out_9, out_10, out_11}));  // open: dp
  DotMatrix #(.matrixcols(8), .matrixrows(1), .dotshape("circle")) dotmatrix_1 (
    .col0(out_4), .col1(out_5), .col2(out_6), .col3(out_7), .col4(out_8), .col5(out_9), .col6(out_10),
    .col7(out_11));

  // Other names for the same wires on the sheet: CLR = Reset

  // Notes on the sheet:
  //   SAP-1 EM LOGISIM
  //   Arquitetura de Computadores I
  //   Grupo:
  //   - Gabriel Jota Lizardo
  //   - Guilherme Oliveira de Rodrigues
  //   - Henrique Oliveira da Cunha Franco
  //   Instruções:
  //   - 0000: pegar o valor
  //   - 0001: somar o valor
  //   - 0010: subtrair o valor
  //   - 0011: pular para instrução especificada
  //   - 0100: Verifica se o valor do acumulador é maior
  //   - 0101: Verifica se o valor do acumulador é menor
  //   - 0110: Verifica se o valor do acumulador é igual
  //   - 0111: Função ainda não adicionada
  //   - 1000: Salva valor do acumulador na RAM
  //   - 1001: Multiplica o valor
  //   - 1010: Divide o valor
  //   - 1110: exibir o valor
  //   - 1111: interromper o circuito
  //   Programas:
  //   - 09 e0 2a e0 1b e0 2c e0 f0 08 06 07 05 00 00 00
  //   - Realiza esta conta: 08 - 06 + 07 - 05 = 04
  //   - 0e 1e e0 8e 1f e0 8f 31 00 00 00 00 00 00 01 01
  //   - Exibe a sequência de fibonacci: 1, 1, 2, 3, 5, 8, 13...
endmodule

module Contador_Programa (
  input  Ar,
  input  [3:0] in_2,
  input  Cp,
  input  nCLK,
  input  nCLR,
  input  Ep,
  output [3:0] Cp_Out
);

  wire not_1_out;
  wire [3:0] counter_1_q;

  not not_1 (not_1_out, nCLR);
  Counter #(.width(4), .max('hf), .trigger("falling")) counter_1 (
    .load(Ar), .D(in_2), .count(Cp), .Q(counter_1_q), .clk(nCLK), .clr(not_1_out));  // open: carry
  assign Cp_Out = Ep ? counter_1_q : 4'bz;  // Controlled_Buffer controlled_buffer_1
endmodule

module REM (
  input  [3:0] in_1,
  input  nLm,
  input  CLK,
  output [3:0] REMOut
);

  wire not_1_out;

  not not_1 (not_1_out, nLm);
  Register #(.width(4)) register_1 (.D(in_1), .en(not_1_out), .Q(REMOut), .clk(CLK));  // open: clr
endmodule

module \Memória_RAM  (
  input  [3:0] in_1,
  input  [7:0] in_2,
  input  nCE,
  input  CLK,
  input  Sv,
  output [7:0] out_6
);

  wire and_1_out, not_1_out, or_1_out;
  wire [7:0] ram_1_data;

  or or_1 (or_1_out, Sv, nCE);
  and and_1 (and_1_out, nCE, not_1_out);
  not not_1 (not_1_out, Sv);
  assign out_6 = nCE ? ram_1_data : 8'bz;  // Controlled_Buffer controlled_buffer_1
  RAM #(.addrWidth(4)) ram_1 (.addr(in_1), .data(ram_1_data), .sel(or_1_out), .clk(CLK), .ld(and_1_out));  // open: clr
  assign ram_1_data = Sv ? in_2 : 8'bz;  // Controlled_Buffer controlled_buffer_2

  // Notes on the sheet:
  //   Operações:
  //   - 09 e0 2a e0 1b e0 2c e0 f0 08 06 07 05 00 00 00
  //   - 08 - 06 + 07 - 05 = 04
  //   - 0e 1e e0 8e 1f e0 8f 31 00 00 00 00 00 00 01 01
  //   - Exibe a sequência de fibonacci: 1, 1, 2, 3, 5, 8, 13...
endmodule

module \Registrador_Instruções  (
  input  [7:0] in_1,
  input  nLi,
  input  CLK,
  input  CLR,
  input  nEi,
  output [7:0] out_6,
  output I4,
  output I5,
  output I6,
  output I7
);

  wire not_1_out, not_2_out;
  wire [3:0] register_1_q;
  wire [7:0] bit_extender_1_out;

  not not_1 (not_1_out, nLi);
  not not_2 (not_2_out, nEi);
  Register register_1 (.D(in_1), .en(not_1_out), .Q({I7, I6, I5, I4, register_1_q}), .clk(CLK), .clr(CLR));
  assign bit_extender_1_out = {{4{1'b0}}, register_1_q};  // Bit_Extender bit_extender_1
  assign out_6 = not_2_out ? bit_extender_1_out : 8'bz;  // Controlled_Buffer controlled_buffer_1
endmodule

module Acumulador (
  input  [7:0] A_In,
  input  nLa,
  input  CLK,
  input  Ea,
  output [7:0] A_Out_ULA,
  output [7:0] A_Out
);

  wire not_1_out;

  not not_1 (not_1_out, nLa);
  Register register_1 (.D(A_In), .en(not_1_out), .Q(A_Out_ULA), .clk(CLK));  // open: clr
  assign A_Out = Ea ? A_Out_ULA : 8'bz;  // Controlled_Buffer controlled_buffer_1
endmodule

module Somador_Subtrator (
  input  Su,
  input  [7:0] B_data,
  input  [7:0] A_data,
  input  Eu,
  input  Gr,
  input  Lo,
  input  Eq,
  input  Mu,
  input  Dv,
  output [7:0] A_dataOut2
);

  wire comparator_1_eq, comparator_1_gt, comparator_1_lt;
  wire [7:0] adder_1_out, bit_extender_1_out, bit_extender_2_out, bit_extender_3_out, divider_1_out,
       multiplier_1_out, xor_1_out;

  assign xor_1_out = {8{Su}} ^ B_data;  // XOR_Gate xor_1, 8 bits wide
  Adder adder_1 (.a(xor_1_out), .b(A_data), .out(adder_1_out), .cin(Su));  // open: cout
  Comparator comparator_1 (.a(A_data), .b(B_data), .gt(comparator_1_gt), .eq(comparator_1_eq), .lt(comparator_1_lt));
  Multiplier multiplier_1 (.a(A_data), .b(B_data), .out(multiplier_1_out));  // open: cin, cout
  Divider divider_1 (.a(A_data), .b(B_data), .out(divider_1_out));  // open: upper, rem
  assign A_dataOut2 = Mu ? multiplier_1_out : 8'bz;  // Controlled_Buffer controlled_buffer_1
  assign A_dataOut2 = Dv ? divider_1_out : 8'bz;  // Controlled_Buffer controlled_buffer_2
  assign A_dataOut2 = Eu ? adder_1_out : 8'bz;  // Controlled_Buffer controlled_buffer_3
  assign bit_extender_1_out = {{7{1'b0}}, comparator_1_gt};  // Bit_Extender bit_extender_1
  assign bit_extender_2_out = {{7{1'b0}}, comparator_1_eq};  // Bit_Extender bit_extender_2
  assign bit_extender_3_out = {{7{1'b0}}, comparator_1_lt};  // Bit_Extender bit_extender_3
  assign A_dataOut2 = Gr ? bit_extender_1_out : 8'bz;  // Controlled_Buffer controlled_buffer_4
  assign A_dataOut2 = Lo ? bit_extender_2_out : 8'bz;  // Controlled_Buffer controlled_buffer_5
  assign A_dataOut2 = Eq ? bit_extender_3_out : 8'bz;  // Controlled_Buffer controlled_buffer_6
endmodule

module Registrador_B (
  input  [7:0] B_dataIn,
  input  nLb,
  input  CLK,
  input  Eb,
  output [7:0] B_out_ULA,
  output [7:0] B_out
);

  wire not_1_out;

  Register register_1 (.D(B_dataIn), .en(not_1_out), .Q(B_out_ULA), .clk(CLK));  // open: clr
  not not_1 (not_1_out, nLb);
  assign B_out = Eb ? B_out_ULA : 8'bz;  // Controlled_Buffer controlled_buffer_1
endmodule

module Controlador_Sequencializador (
  input  CLK,
  input  CLR,
  input  I7,
  input  I6,
  input  I5,
  input  I4,
  output Ep,
  output Cp,
  output HLT,
  output nLm,
  output nCE,
  output nEl,
  output nLa,
  output Ea,
  output Su,
  output Eu,
  output nLb,
  output nLo,
  output nLl,
  output Ar,
  output Gr,
  output Lo,
  output Eq,
  output Eb,
  output Sv,
  output Mu,
  output Dv
);

  wire and_1_out, and_2_out, and_3_out, c39_1_out_7, c39_1_out_8, c39_1_out_9, c39_1_out_10, c40_1_out_7,
       c40_1_out_8, c40_1_out_9, c40_1_out_10, c41_1_out_8, c41_1_out_9, c41_1_out_10, c41_1_out_11,
       c41_2_out_8, c41_2_out_10, c41_2_out_11, c43_1_out_6, c43_1_out_7, c43_1_out_8, c44_1_out_9,
       c44_1_out_10, c45_1_out_7, c45_1_out_8, c46_1_out_6, contadoremanel_1_out_7, contadoremanel_1_out_8,
       contadoremanel_1_out_9, contadoremanel_1_out_10, decodificador_1_add, decodificador_1_div,
       decodificador_1_equ, decodificador_1_gre, decodificador_1_jif, decodificador_1_jmp,
       decodificador_1_lda, decodificador_1_low, decodificador_1_mut, decodificador_1_out,
       decodificador_1_sav, decodificador_1_sub, j_k_ff_1_q, nor_1_out, or_1_out, or_2_out, or_3_out,
       or_4_out, or_5_out, or_7_out, or_9_out, reset, tCE, tEi, tEi3, tLa;

  Decodificador decodificador_1 (
    .LDA(decodificador_1_lda), .ADD(decodificador_1_add), .SUB(decodificador_1_sub),
    .OUT(decodificador_1_out), .HLT(HLT), .l7(I7), .l6(I6), .l5(I5), .l4(I4), .JMP(decodificador_1_jmp),
    .GRE(decodificador_1_gre), .LOW(decodificador_1_low), .EQU(decodificador_1_equ),
    .JIF(decodificador_1_jif), .SAV(decodificador_1_sav), .MUT(decodificador_1_mut), .DIV(decodificador_1_div));
  C39 c39_1 (
    ._1(decodificador_1_lda), ._4(decodificador_1_add), ._9(decodificador_1_sub),
    ._10(contadoremanel_1_out_8), ._12(decodificador_1_lda), ._13(contadoremanel_1_out_9),
    .out_7(c39_1_out_7), .out_8(c39_1_out_8), .out_9(c39_1_out_9), .out_10(c39_1_out_10));
  J_K_Flip_Flop j_k_ff_1 (.Q(j_k_ff_1_q), .preset(CLR), .reset(CLK));  // open: J, clk, K, Qn, en
  C40 c40_1 (
    ._1(decodificador_1_add), ._4(decodificador_1_sub), ._5(contadoremanel_1_out_9),
    ._9(decodificador_1_lda), ._12(decodificador_1_add), ._13(contadoremanel_1_out_8), .out_7(c40_1_out_7),
    .out_8(c40_1_out_8), .out_9(c40_1_out_9), .out_10(c40_1_out_10));
  C44 c44_1 (
    .in_1(Ep), .in_2(c39_1_out_7), .in_3(c39_1_out_8), .in_4(c39_1_out_9), .in_5(contadoremanel_1_out_7),
    .in_6(c39_1_out_10), .in_7(c40_1_out_7), .in_8(c40_1_out_8), .out_9(c44_1_out_9), .out_10(c44_1_out_10));
  or or_1 (or_1_out, tEi3, tEi, c44_1_out_9);
  or or_2 (or_2_out, c44_1_out_10, tCE);
  not not_1 (nLm, or_1_out);
  not not_2 (nCE, or_2_out);
  ContadorEmAnel contadoremanel_1 (
    .in_1(CLK), .in_2(1'b0), .in_3(or_5_out), .in_4(j_k_ff_1_q), .out_5(Ep), .out_6(Cp),
    .out_7(contadoremanel_1_out_7), .out_8(contadoremanel_1_out_8), .out_9(contadoremanel_1_out_9),
    .out_10(contadoremanel_1_out_10));
  C41 c41_1 (
    ._1(decodificador_1_sub), ._2(contadoremanel_1_out_8), ._4(decodificador_1_lda),
    ._5(contadoremanel_1_out_9), ._9(decodificador_1_add), ._12(decodificador_1_sub),
    ._13(contadoremanel_1_out_10), .out_8(c41_1_out_8), .out_9(c41_1_out_9), .out_10(c41_1_out_10),
    .out_11(c41_1_out_11));
  C45 c45_1 (
    .in_1(c40_1_out_9), .in_2(c40_1_out_10), .in_3(c41_1_out_8), .in_4(c41_1_out_9), .in_5(c41_1_out_10),
    .in_6(c41_1_out_11), .out_7(c45_1_out_7), .out_8(c45_1_out_8));
  C41 c41_2 (
    ._1(decodificador_1_out), ._2(contadoremanel_1_out_8), ._4(decodificador_1_sub),
    ._5(contadoremanel_1_out_10), ._9(decodificador_1_add), ._12(decodificador_1_sub),
    ._13(contadoremanel_1_out_10), .out_8(c41_2_out_8), .out_9(Su), .out_10(c41_2_out_10),
    .out_11(c41_2_out_11));
  or or_3 (or_3_out, c45_1_out_8, tLa);
  or or_4 (or_4_out, tEi3, Ar, tEi, c45_1_out_7);
  not not_3 (nLa, or_3_out);
  not not_4 (nEl, or_4_out);
  or or_5 (or_5_out, reset, nor_1_out);
  C46 c46_1 (
    .in_1(c41_2_out_10), .in_2(c41_2_out_11), .in_3(c43_1_out_6), .in_4(c43_1_out_7), .out_5(Eu),
    .out_6(c46_1_out_6));
  or or_6 (Ea, c41_2_out_8, Sv);
  C43 c43_1 (
    ._1(decodificador_1_add), ._4(decodificador_1_sub), ._5(contadoremanel_1_out_9),
    ._9(decodificador_1_out), ._10(contadoremanel_1_out_8), .out_6(c43_1_out_6), .out_7(c43_1_out_7),
    .out_8(c43_1_out_8));
  or or_7 (or_7_out, c46_1_out_6, tCE);
  not not_5 (nLb, or_7_out);
  nor nor_1 (nor_1_out, Ep, Cp, contadoremanel_1_out_7, contadoremanel_1_out_8, contadoremanel_1_out_9, contadoremanel_1_out_10);
  not not_6 (nLl, contadoremanel_1_out_7);
  not not_7 (nLo, c43_1_out_8);
  and and_1 (and_1_out, contadoremanel_1_out_10, decodificador_1_lda);
  and and_2 (and_2_out, decodificador_1_jmp, contadoremanel_1_out_9);
  and and_3 (and_3_out, decodificador_1_out, contadoremanel_1_out_9);
  or or_8 (reset, and_1_out, and_3_out, and_2_out);
  or or_9 (or_9_out, decodificador_1_mut, decodificador_1_gre, decodificador_1_low, decodificador_1_equ, decodificador_1_div);
  and and_4 (Ar, decodificador_1_jmp, contadoremanel_1_out_8);
  and and_5 (Gr, decodificador_1_gre, contadoremanel_1_out_10);
  and and_6 (tEi, contadoremanel_1_out_8, or_9_out);
  and and_7 (Eq, contadoremanel_1_out_10, decodificador_1_equ);
  and and_8 (Lo, decodificador_1_low, contadoremanel_1_out_10);
  and and_9 (tCE, or_9_out, contadoremanel_1_out_9);
  and and_10 (tLa, or_9_out, contadoremanel_1_out_10);
  and and_11 (tEi3, decodificador_1_sav, contadoremanel_1_out_8);
  and and_12 (Sv, decodificador_1_sav, contadoremanel_1_out_9);
  and and_13 (Mu, decodificador_1_mut, contadoremanel_1_out_10);
  and and_14 (Dv, contadoremanel_1_out_10, decodificador_1_div);

  assign Eb = 1'b0;

  // Other names for the same wires on the sheet: tEa = Sv; tEi2 = Ar; tLb = tCE; tLm = tEi; tLm2 = tEi3
endmodule

module Decodificador (
  input  l7,
  input  l6,
  input  l5,
  input  l4,
  output LDA,
  output ADD,
  output SUB,
  output OUT,
  output HLT,
  output JMP,
  output GRE,
  output LOW,
  output EQU,
  output JIF,
  output SAV,
  output MUT,
  output DIV
);

  wire and_1_out, and_2_out, and_3_out, and_4_out, and_5_out, and_6_out, and_7_out, and_8_out, and_9_out,
       and_10_out, and_11_out, and_12_out, and_13_out, not_1_out, not_2_out, not_3_out, not_4_out;

  not not_1 (not_1_out, l7);
  not not_2 (not_2_out, l6);
  not not_3 (not_3_out, l5);
  not not_4 (not_4_out, l4);
  buf buffer_1 (LDA, and_1_out);
  and and_1 (and_1_out, not_1_out, not_2_out, not_3_out, not_4_out);
  and and_2 (and_2_out, not_1_out, not_2_out, not_3_out, l4);
  buf buffer_2 (ADD, and_2_out);
  buf buffer_3 (SUB, and_3_out);
  and and_3 (and_3_out, not_1_out, not_2_out, l5, not_4_out);
  and and_4 (and_4_out, l7, l6, l5, not_4_out);
  buf buffer_4 (OUT, and_4_out);
  and and_5 (and_5_out, l7, l6, l5, l4);
  buf buffer_5 (HLT, and_5_out);
  buf buffer_6 (JMP, and_6_out);
  and and_6 (and_6_out, not_1_out, not_2_out, l5, l4);
  and and_7 (and_7_out, not_1_out, l6, not_3_out, not_4_out);
  buf buffer_7 (GRE, and_7_out);
  buf buffer_8 (LOW, and_8_out);
  and and_8 (and_8_out, not_1_out, l6, not_3_out, l4);
  buf buffer_9 (EQU, and_9_out);
  and and_9 (and_9_out, not_1_out, l6, l5, not_4_out);
  buf buffer_10 (JIF, and_10_out);
  and and_10 (and_10_out, not_1_out, l6, l5, l4);
  and and_11 (and_11_out, l7, not_2_out, not_3_out, not_4_out);
  buf buffer_11 (SAV, and_11_out);
  buf buffer_12 (MUT, and_12_out);
  and and_12 (and_12_out, l7, not_2_out, not_3_out, l4);
  buf buffer_13 (DIV, and_13_out);
  and and_13 (and_13_out, l7, not_2_out, l5, not_4_out);
endmodule

module C39 (
  input  _1,
  input  _4,
  input  _9,
  input  _10,
  input  _13,
  input  _12,
  output out_7,
  output out_8,
  output out_9,
  output out_10
);

  and and_1 (out_7, _1, _10);
  and and_2 (out_9, _9, _10);
  and and_3 (out_8, _4, _10);
  and and_4 (out_10, _12, _13);
endmodule

module C40 (
  input  _1,
  input  _4,
  input  _5,
  input  _9,
  input  _12,
  input  _13,
  output out_7,
  output out_8,
  output out_9,
  output out_10
);

  and and_1 (out_7, _1, _5);
  and and_2 (out_8, _4, _5);
  and and_3 (out_9, _9, _13);
  and and_4 (out_10, _12, _13);
endmodule

module C41 (
  input  _4,
  input  _5,
  input  _12,
  input  _13,
  input  _1,
  input  _2,
  input  _9,
  output out_8,
  output out_9,
  output out_10,
  output out_11
);

  and and_1 (out_8, _1, _2);
  and and_2 (out_9, _4, _5);
  and and_3 (out_10, _9, _13);
  and and_4 (out_11, _12, _13);
endmodule

module C43 (
  input  _1,
  input  _4,
  input  _5,
  input  _9,
  input  _10,
  output out_6,
  output out_7,
  output out_8
);

  and and_1 (out_6, _1, _5);
  and and_2 (out_7, _4, _5);
  and and_3 (out_8, _9, _10);
endmodule

module C44 (
  input  in_1,
  input  in_2,
  input  in_3,
  input  in_4,
  input  in_5,
  input  in_6,
  input  in_7,
  input  in_8,
  output out_9,
  output out_10
);

  or or_1 (out_9, in_1, in_2, in_3, in_4);
  or or_2 (out_10, in_5, in_6, in_7, in_8);
endmodule

module C45 (
  input  in_1,
  input  in_2,
  input  in_3,
  input  in_4,
  input  in_5,
  input  in_6,
  output out_7,
  output out_8
);

  or or_1 (out_7, in_1, in_2, in_3);
  or or_2 (out_8, in_4, in_5, in_6);
endmodule

module C46 (
  input  in_1,
  input  in_2,
  input  in_3,
  input  in_4,
  output out_5,
  output out_6
);

  or or_1 (out_5, in_1, in_2);
  or or_2 (out_6, in_3, in_4);
endmodule

module \Indicação_Visual  (
  input  [7:0] Input,
  input  nLo,
  input  CLK,
  input  CLR,
  output [7:0] Output
);

  wire not_1_out;

  not not_1 (not_1_out, nLo);
  Register register_1 (.D(Input), .en(not_1_out), .Q(Output), .clk(CLK), .clr(CLR));
endmodule

module ContadorEmAnel (
  input  in_1,
  input  in_2,
  input  in_3,
  input  in_4,
  output out_5,
  output out_6,
  output out_7,
  output out_8,
  output out_9,
  output out_10
);

  wire or_1_out, or_2_out, or_3_out, or_4_out, or_5_out;

  D_Flip_Flop d_ff_1 (.clk(in_1), .D(in_2), .Q(out_5), .preset(in_3), .en(1'b1), .reset(in_4));  // open: Qn
  D_Flip_Flop d_ff_2 (.clk(in_1), .D(out_5), .Q(out_6), .en(1'b1), .reset(or_1_out));  // open: Qn, preset
  or or_1 (or_1_out, in_3, in_4);
  D_Flip_Flop d_ff_3 (.clk(in_1), .D(out_6), .Q(out_7), .en(1'b1), .reset(or_2_out));  // open: Qn, preset
  or or_2 (or_2_out, in_3, in_4);
  D_Flip_Flop d_ff_4 (.clk(in_1), .D(out_7), .Q(out_8), .en(1'b1), .reset(or_3_out));  // open: Qn, preset
  or or_3 (or_3_out, in_3, in_4);
  D_Flip_Flop d_ff_5 (.clk(in_1), .D(out_8), .Q(out_9), .en(1'b1), .reset(or_4_out));  // open: Qn, preset
  or or_4 (or_4_out, in_3, in_4);
  D_Flip_Flop d_ff_6 (.clk(in_1), .D(out_9), .Q(out_10), .en(1'b1), .reset(or_5_out));  // open: Qn, preset
  or or_5 (or_5_out, in_3, in_4);
endmodule
